// Logisim project S2.circ as structural Verilog: 1 circuit, main circuit main
module main (
  input  Set_Time
);

  wire and_1_out, and_2_out, and_3_out, and_4_out, clock_1_out, m_plus_out, or_1_out, xor_1_out;
  wire [3:0] j_k_ff_1_q, j_k_ff_2_q;

  Clock #(.phaseOffset(1)) clock_1 (.out(clock_1_out));
  and and_1 (and_1_out, Set_Time, m_plus_out);
  or or_1 (or_1_out, clock_1_out, Set_Time);
  J_K_Flip_Flop #(.trigger("falling")) j_k_ff_1 (
    .J(1'b1), .K(1'b1), .clk(and_4_out), .Q(j_k_ff_1_q[0]), .reset(and_2_out));  // open: Qn, preset
  xor xor_1 (xor_1_out, and_1_out, or_1_out);
  LED led_1 (.in(j_k_ff_1_q[0]));
  J_K_Flip_Flop #(.trigger("falling")) j_k_ff_2 (
    .J(1'b1), .K(1'b1), .clk(xor_1_out), .Q(j_k_ff_2_q[0]), .reset(and_3_out));  // open: Qn, preset
  J_K_Flip_Flop #(.trigger("falling")) j_k_ff_3 (
    .J(1'b1), .K(1'b1), .clk(j_k_ff_1_q[0]), .Q(j_k_ff_1_q[1]), .reset(and_2_out));  // open: Qn, preset
  J_K_Flip_Flop #(.trigger("falling")) j_k_ff_4 (
    .J(1'b1), .K(1'b1), .clk(j_k_ff_2_q[0]), .Q(j_k_ff_2_q[1]), .reset(and_3_out));  // open: Qn, preset
  LED led_2 (.in(j_k_ff_2_q[0]));
  J_K_Flip_Flop #(.trigger("falling")) j_k_ff_5 (
    .J(1'b1), .K(1'b1), .clk(j_k_ff_1_q[1]), .Q(j_k_ff_1_q[2]), .reset(and_2_out));  // open: Qn, preset
  LED led_3 (.in(j_k_ff_1_q[1]));
  LED led_4 (.in(j_k_ff_2_q[1]));
  LED led_5 (.in(j_k_ff_1_q[2]));
  J_K_Flip_Flop #(.trigger("falling")) j_k_ff_6 (
    .J(1'b1), .K(1'b1), .clk(j_k_ff_2_q[1]), .Q(j_k_ff_2_q[2]), .reset(and_3_out));  // open: Qn, preset
  and and_2 (and_2_out, j_k_ff_1_q[1], j_k_ff_1_q[2]);
  J_K_Flip_Flop #(.trigger("falling")) j_k_ff_7 (
    .J(1'b1), .K(1'b1), .clk(j_k_ff_1_q[2]), .Q(j_k_ff_1_q[3]), .reset(and_2_out));  // open: Qn, preset
  LED led_6 (.in(j_k_ff_2_q[2]));
  LED led_7 (.in(j_k_ff_1_q[3]));
  and and_3 (and_3_out, j_k_ff_2_q[1], j_k_ff_2_q[3]);
  J_K_Flip_Flop #(.trigger("falling")) j_k_ff_8 (
    .J(1'b1), .K(1'b1), .clk(j_k_ff_2_q[2]), .Q(j_k_ff_2_q[3]), .reset(and_3_out));  // open: Qn, preset
  LED led_8 (.in(j_k_ff_2_q[3]));
  and and_4 (and_4_out, j_k_ff_2_q[0], j_k_ff_2_q[3]);
  Button m_plus (.out(m_plus_out));
  Hex_Digit_Display hex_digit_display_1 (.value(j_k_ff_1_q));  // open: dp
  Hex_Digit_Display hex_digit_display_2 (.value(j_k_ff_2_q));  // open: dp
endmodule
