// Logisim project S3.circ as structural Verilog: 1 circuit, main circuit main
module main (
  input  Set_Time
);

  wire and_1_out, and_2_out, and_3_out, and_4_out, and_5_out, and_6_out, and_7_out, clock_1_out, h_plus_out,
       j_k_ff_9_q, not_1_out, not_2_out, not_3_out, or_1_out, or_2_out, or_3_out, xor_1_out;
  wire [3:0] j_k_ff_1_q, j_k_ff_2_q;

  Clock #(.phaseOffset(1)) clock_1 (.out(clock_1_out));
  and and_1 (and_1_out, h_plus_out, Set_Time);
  or or_1 (or_1_out, Set_Time, clock_1_out);
  xor xor_1 (xor_1_out, and_1_out, or_1_out);
  J_K_Flip_Flop #(.trigger("falling")) j_k_ff_1 (
    .J(1'b1), .K(1'b1), .clk(xor_1_out), .Q(j_k_ff_1_q[0]));  // open: Qn, preset, reset
  J_K_Flip_Flop #(.trigger("falling")) j_k_ff_2 (
    .J(1'b1), .K(1'b1), .clk(and_4_out), .Q(j_k_ff_2_q[0]), .reset(or_2_out));  // open: Qn, preset
  LED led_1 (.in(j_k_ff_1_q[0]));
  J_K_Flip_Flop #(.trigger("falling")) j_k_ff_3 (
    .J(1'b1), .K(1'b1), .clk(j_k_ff_2_q[0]), .Q(j_k_ff_2_q[1]), .reset(or_2_out));  // open: Qn, preset
  LED led_2 (.in(j_k_ff_2_q[0]));
  J_K_Flip_Flop #(.trigger("falling")) j_k_ff_4 (
    .J(1'b1), .K(1'b1), .clk(j_k_ff_1_q[0]), .Q(j_k_ff_1_q[1]), .reset(or_3_out));  // open: Qn, preset
  LED led_3 (.in(j_k_ff_2_q[1]));
  and and_2 (and_2_out, j_k_ff_1_q[0], j_k_ff_1_q[1]);
  J_K_Flip_Flop #(.trigger("falling")) j_k_ff_5 (
    .J(1'b1), .K(1'b1), .clk(j_k_ff_1_q[1]), .Q(j_k_ff_1_q[2]), .reset(or_3_out));  // open: Qn, preset
  LED led_4 (.in(j_k_ff_1_q[1]));
  not not_1 (not_1_out, j_k_ff_2_q[1]);
  J_K_Flip_Flop #(.trigger("falling")) j_k_ff_6 (
    .J(1'b1), .K(1'b1), .clk(j_k_ff_2_q[1]), .Q(j_k_ff_2_q[2]), .reset(or_2_out));  // open: Qn, preset
  LED led_5 (.in(j_k_ff_1_q[2]));
  and and_3 (and_3_out, j_k_ff_2_q[0], not_1_out);
  not not_2 (not_2_out, j_k_ff_2_q[2]);
  LED led_6 (.in(j_k_ff_2_q[2]));
  and and_4 (and_4_out, j_k_ff_1_q[0], j_k_ff_1_q[3]);
  J_K_Flip_Flop #(.trigger("falling")) j_k_ff_7 (
    .J(1'b1), .K(1'b1), .clk(j_k_ff_1_q[2]), .Q(j_k_ff_1_q[3]), .reset(or_3_out));  // open: Qn, preset
  and and_5 (and_5_out, j_k_ff_2_q[1], not_2_out);
  J_K_Flip_Flop #(.trigger("falling")) j_k_ff_8 (
    .J(1'b1), .K(1'b1), .clk(j_k_ff_2_q[2]), .Q(j_k_ff_2_q[3]), .reset(or_2_out));  // open: Qn, preset
  LED led_7 (.in(j_k_ff_1_q[3]));
  LED led_8 (.in(j_k_ff_2_q[3]));
  and and_6 (and_6_out, j_k_ff_1_q[1], j_k_ff_1_q[3]);
  or or_2 (or_2_out, and_5_out, and_7_out);
  or or_3 (or_3_out, and_6_out, and_7_out);
  Button h_plus (.out(h_plus_out));
  J_K_Flip_Flop j_k_ff_9 (.J(1'b1), .K(1'b1), .clk(and_7_out), .Q(j_k_ff_9_q));  // open: Qn, preset, reset
  Hex_Digit_Display hex_digit_display_1 (.value(j_k_ff_2_q));  // open: dp
  Hex_Digit_Display hex_digit_display_2 (.value(j_k_ff_1_q));  // open: dp
  and and_7 (and_7_out, and_2_out, and_3_out);
  LED PM (.in(not_3_out));
  LED AM (.in(j_k_ff_9_q));
  not not_3 (not_3_out, j_k_ff_9_q);
endmodule
