// Logisim project S4.circ as structural Verilog: 1 circuit, main circuit main
module main (
  input  Set_Time
);

  wire and_1_out, and_2_out, and_3_out, and_4_out, and_5_out, and_6_out, and_7_out, and_8_out, and_9_out,
       and_10_out, and_11_out, and_12_out, and_13_out, clock_1_out, h_plus_out, j_k_ff_9_q, m_plus_out,
       not_1_out, not_2_out, not_3_out, or_1_out, or_2_out, or_3_out, or_4_out, xor_1_out, xor_2_out;
  wire [3:0] j_k_ff_1_q, j_k_ff_2_q, j_k_ff_10_q, j_k_ff_11_q;

  and and_1 (and_1_out, Set_Time, h_plus_out);
  or or_1 (or_1_out, Set_Time, and_13_out);
  xor xor_1 (xor_1_out, and_1_out, or_1_out);
  J_K_Flip_Flop #(.trigger("falling")) j_k_ff_1 (
    .J(1'b1), .K(1'b1), .clk(xor_1_out), .Q(j_k_ff_1_q[0]));  // open: Qn, preset, reset
  J_K_Flip_Flop #(.trigger("falling")) j_k_ff_2 (
    .J(1'b1), .K(1'b1), .clk(and_4_out), .Q(j_k_ff_2_q[0]), .reset(or_2_out));  // open: Qn, preset
  LED led_1 (.in(j_k_ff_1_q[0]));
  LED led_2 (.in(j_k_ff_2_q[0]));
  J_K_Flip_Flop #(.trigger("falling")) j_k_ff_3 (
    .J(1'b1), .K(1'b1), .clk(j_k_ff_1_q[0]), .Q(j_k_ff_1_q[1]), .reset(or_3_out));  // open: Qn, preset
  J_K_Flip_Flop #(.trigger("falling")) j_k_ff_4 (
    .J(1'b1), .K(1'b1), .clk(j_k_ff_2_q[0]), .Q(j_k_ff_2_q[1]), .reset(or_2_out));  // open: Qn, preset
  LED led_3 (.in(j_k_ff_1_q[1]));
  not not_1 (not_1_out, j_k_ff_2_q[1]);
  J_K_Flip_Flop #(.trigger("falling")) j_k_ff_5 (
    .J(1'b1), .K(1'b1), .clk(j_k_ff_2_q[1]), .Q(j_k_ff_2_q[2]), .reset(or_2_out));  // open: Qn, preset
  LED led_4 (.in(j_k_ff_2_q[1]));
  and and_2 (and_2_out, j_k_ff_1_q[0], j_k_ff_1_q[1]);
  J_K_Flip_Flop #(.trigger("falling")) j_k_ff_6 (
    .J(1'b1), .K(1'b1), .clk(j_k_ff_1_q[1]), .Q(j_k_ff_1_q[2]), .reset(or_3_out));  // open: Qn, preset
  not not_2 (not_2_out, j_k_ff_2_q[2]);
  LED led_5 (.in(j_k_ff_2_q[2]));
  J_K_Flip_Flop #(.trigger("falling")) j_k_ff_7 (
    .J(1'b1), .K(1'b1), .clk(j_k_ff_1_q[2]), .Q(j_k_ff_1_q[3]), .reset(or_3_out));  // open: Qn, preset
  LED led_6 (.in(j_k_ff_1_q[2]));
  and and_3 (and_3_out, j_k_ff_2_q[0], not_1_out);
  J_K_Flip_Flop #(.trigger("falling")) j_k_ff_8 (
    .J(1'b1), .K(1'b1), .clk(j_k_ff_2_q[2]), .Q(j_k_ff_2_q[3]), .reset(or_2_out));  // open: Qn, preset
  and and_4 (and_4_out, j_k_ff_1_q[0], j_k_ff_1_q[3]);
  LED led_7 (.in(j_k_ff_1_q[3]));
  and and_5 (and_5_out, j_k_ff_2_q[1], not_2_out);
  LED led_8 (.in(j_k_ff_2_q[3]));
  and and_6 (and_6_out, j_k_ff_1_q[1], j_k_ff_1_q[3]);
  or or_2 (or_2_out, and_5_out, and_7_out);
  or or_3 (or_3_out, and_6_out, and_7_out);
  and and_7 (and_7_out, and_2_out, and_3_out);
  J_K_Flip_Flop j_k_ff_9 (.J(1'b1), .K(1'b1), .clk(and_7_out), .Q(j_k_ff_9_q));  // open: Qn, preset, reset
  not not_3 (not_3_out, j_k_ff_9_q);
  Button h_plus (.out(h_plus_out));
  LED AM (.in(j_k_ff_9_q));
  LED PM (.in(not_3_out));
  Hex_Digit_Display hex_digit_display_1 (.value(j_k_ff_2_q));  // open: dp
  Hex_Digit_Display hex_digit_display_2 (.value(j_k_ff_1_q));  // open: dp
  Clock #(.phaseOffset(1)) clock_1 (.out(clock_1_out));
  Hex_Digit_Display hex_digit_display_3 (.value(j_k_ff_10_q));  // open: dp
  Hex_Digit_Display hex_digit_display_4 (.value(j_k_ff_11_q));  // open: dp
  Button m_plus (.out(m_plus_out));
  and and_8 (and_8_out, Set_Time, m_plus_out);
  or or_4 (or_4_out, clock_1_out, Set_Time);
  J_K_Flip_Flop #(.trigger("falling")) j_k_ff_10 (
    .J(1'b1), .K(1'b1), .clk(and_12_out), .Q(j_k_ff_10_q[0]), .reset(and_9_out));  // open: Qn, preset
  LED led_9 (.in(j_k_ff_10_q[0]));
  J_K_Flip_Flop #(.trigger("falling")) j_k_ff_11 (
    .J(1'b1), .K(1'b1), .clk(xor_2_out), .Q(j_k_ff_11_q[0]), .reset(and_10_out));  // open: Qn, preset
  xor xor_2 (xor_2_out, and_8_out, or_4_out);
  J_K_Flip_Flop #(.trigger("falling")) j_k_ff_12 (
    .J(1'b1), .K(1'b1), .clk(j_k_ff_10_q[0]), .Q(j_k_ff_10_q[1]), .reset(and_9_out));  // open: Qn, preset
  LED led_10 (.in(j_k_ff_11_q[0]));
  LED led_11 (.in(j_k_ff_10_q[1]));
  J_K_Flip_Flop #(.trigger("falling")) j_k_ff_13 (
    .J(1'b1), .K(1'b1), .clk(j_k_ff_11_q[0]), .Q(j_k_ff_11_q[1]), .reset(and_10_out));  // open: Qn, preset
  J_K_Flip_Flop #(.trigger("falling")) j_k_ff_14 (
    .J(1'b1), .K(1'b1), .clk(j_k_ff_10_q[1]), .Q(j_k_ff_10_q[2]), .reset(and_9_out));  // open: Qn, preset
  LED led_12 (.in(j_k_ff_11_q[1]));
  and and_9 (and_9_out, j_k_ff_10_q[1], j_k_ff_10_q[2]);
  J_K_Flip_Flop #(.trigger("falling")) j_k_ff_15 (
    .J(1'b1), .K(1'b1), .clk(j_k_ff_10_q[2]), .Q(j_k_ff_10_q[3]), .reset(and_9_out));  // open: Qn, preset
  LED led_13 (.in(j_k_ff_10_q[2]));
  J_K_Flip_Flop #(.trigger("falling")) j_k_ff_16 (
    .J(1'b1), .K(1'b1), .clk(j_k_ff_11_q[1]), .Q(j_k_ff_11_q[2]), .reset(and_10_out));  // open: Qn, preset
  LED led_14 (.in(j_k_ff_10_q[3]));
  J_K_Flip_Flop #(.trigger("falling")) j_k_ff_17 (
    .J(1'b1), .K(1'b1), .clk(j_k_ff_11_q[2]), .Q(j_k_ff_11_q[3]), .reset(and_10_out));  // open: Qn, preset
  LED led_15 (.in(j_k_ff_11_q[2]));
  and and_10 (and_10_out, j_k_ff_11_q[1], j_k_ff_11_q[3]);
  LED led_16 (.in(j_k_ff_11_q[3]));
  and and_11 (and_11_out, j_k_ff_10_q[2], j_k_ff_10_q[0]);
  and and_12 (and_12_out, j_k_ff_11_q[0], j_k_ff_11_q[3]);
  and and_13 (and_13_out, and_12_out, and_11_out);
endmodule
